# Fritzing sketch BOP_BOARD (saved by Fritzing 0.9.3b)
circuit board: 1.8cm x 1.25cm
breadboards: 1

parts:
  U1 = ATTINY45 [package=so]
  R1 = Resistor [tolerance=±5% resistance=220 package="0603 [SMD]"]
  R3 = Resistor [tolerance=±5% resistance=220 package="0603 [SMD]"]
  C1 = Ceramic Capacitor [capacitance=100nF package="0603 [SMD, multilayer]"]
  R4 = Resistor [tolerance=±5% resistance=220 package="0603 [SMD]"]
  R5 = Resistor [tolerance=±5% resistance=220 package="0603 [SMD]"]

nets:
  N1: U1.PB5(NRES), R1.Pin_0
  N2: U1.GND, R3.Pin_1, C1.0
  N3: U1.PB0(MOSI), R5.Pin_1
  N4: U1.PB1(MISO), R4.Pin_0
  N5: U1.VCC, R1.Pin_1, C1.1
