# Fritzing sketch BOP_BOARD_v2 (saved by Fritzing 0.9.3b)
circuit board: 1.65cm x 1.2cm
breadboards: 1

parts:
  U1 = ATTINY45 [package=so]
  R1 = Resistor [tolerance=±5% resistance=220 package="0603 [SMD]"]
  R3 = Resistor [tolerance=±5% resistance=220 package="0603 [SMD]"]
  C1 = Ceramic Capacitor [capacitance=100nF package="0603 [SMD, multilayer]"]
  R4 = Resistor [tolerance=±5% resistance=220 package="0603 [SMD]"]
  R5 = Resistor [tolerance=±5% resistance=220 package="0603 [SMD]"]
  Q1 = TRANSISTOR_NPN [package=sot23-3]
  Q2 = TRANSISTOR_NPN [package=sot23-3]

nets:
  N1: U1.PB5(NRES), R1.Pin_0
  N2: U1.GND, R3.Pin_1, C1.0, Q1.E, Q2.E
  N3: U1.PB0(MOSI), R5.Pin_0
  N4: U1.PB1(MISO), R4.Pin_0
  N5: U1.VCC, R1.Pin_1, C1.1
  N6: R4.Pin_1, Q1.B
  N7: R5.Pin_1, Q2.B
